// Logisim project lcpu.circ as structural Verilog
module main (
);

  wire ALU_cout, ALU_eq, ALU_gt, ALU_lt, ALU_zero, clock_1_out, CU_cin, CU_dset, CU_fetch, CU_fset, CU_iset,
       CU_pcload, CU_sinv, CU_ssel, CU_tinv, CU_tsel, CU_write, not_1_out, or_1_out;
  wire [1:0] CU_dsel, CU_pcop;
  wire [2:0] ID_dreg, ID_sreg, ID_treg;
  wire [3:0] CU_aop;
  wire [6:0] ID_op;
  wire [15:0] ALU_dval, imm_q, multiplexer_1_out, multiplexer_2_out, multiplexer_3_out, PC_pc, ram_1_data,
       RF_sval, RF_tval;

  pc_16bit PC (.pcop(CU_pcop), .pcset(CU_pcload), .clock(clock_1_out), .pc(PC_pc));  // open: addr, reset, pc_1
  // Probe on PC_pc
  RAM #(.addrWidth(16), .dataWidth(16)) ram_1 (
    .addr(PC_pc), .data(ram_1_data), .clk(clock_1_out), .ld(not_1_out));  // open: sel, clr
  not not_1 (not_1_out, CU_write);
  Clock clock_1 (.out(clock_1_out));
  // Probe on ram_1_data
  id_16bit ID (
    .inst(ram_1_data), .fetch(CU_fetch), .clock(clock_1_out), .op(ID_op), .dreg(ID_dreg), .sreg(ID_sreg),
    .treg(ID_treg));
  // Probe on ID_op
  cu_7bit CU (
    .cop(ID_op), .ssel(CU_ssel), .tsel(CU_tsel), .cin(CU_cin), .sinv(CU_sinv), .tinv(CU_tinv), .aop(CU_aop),
    .dset(CU_dset), .fset(CU_fset), .iset(CU_iset), .fetch(CU_fetch), .pcload(CU_pcload), .pcop(CU_pcop),
    .write(CU_write), .dsel(CU_dsel));  // open: timm
  Register #(.width(16)) imm (.D(ram_1_data), .en(CU_iset), .Q(imm_q), .clk(clock_1_out));  // open: clr
  Multiplexer #(.select(2), .width(16)) multiplexer_1 (
    .in0(imm_q), .in1(ram_1_data), .in2(ALU_dval), .out(multiplexer_1_out), .sel(CU_dsel));  // open: in3, en
  registerFile_8x16bit RF (
    .dreg(ID_dreg), .sreg(ID_sreg), .treg(ID_treg), .dval(multiplexer_1_out), .dset(CU_dset),
    .clock(clock_1_out), .sval(RF_sval), .tval(RF_tval));  // open: reg0, reg1, reg2, reg3, reg4, reg5, reg6, reg7
  // Probe on ID_treg
  Multiplexer #(.width(16)) multiplexer_2 (
    .in0(RF_sval), .in1(imm_q), .out(multiplexer_2_out), .sel(CU_ssel));  // open: en
  Multiplexer #(.width(16)) multiplexer_3 (
    .in0(RF_tval), .in1({16{1'b0}}), .out(multiplexer_3_out), .sel(or_1_out));  // open: en
  // Probe on or_1_out
  or or_1 (or_1_out, CU_tsel, ID_treg[0]);
  // Probe on multiplexer_2_out
  // Probe on multiplexer_3_out
  alu_16bit ALU (
    .sval(multiplexer_2_out), .tval(multiplexer_3_out), .cin(CU_cin), .sinv(CU_sinv), .tinv(CU_tinv),
    .aop(CU_aop), .gt(ALU_gt), .eq(ALU_eq), .lt(ALU_lt), .cout(ALU_cout), .zero(ALU_zero), .dval(ALU_dval));
  // Probe on ALU_dval
  // Probe on CU_aop
  fu fu_1 (
    .gt(ALU_gt), .eq(ALU_eq), .lt(ALU_lt), .cout(ALU_cout), .zero(ALU_zero), .fset(CU_fset));  // open: br, clock, gt_2, eq_2, lt_2, cout_2, zero_2, br_2
endmodule

module registerFile_8x16bit (
  input  [2:0] dreg,
  input  clock,
  input  [2:0] sreg,
  input  [2:0] treg,
  input  dset,
  input  [15:0] dval,
  output [15:0] reg0,
  output [15:0] reg1,
  output [15:0] reg2,
  output [15:0] reg3,
  output [15:0] reg4,
  output [15:0] reg5,
  output [15:0] reg6,
  output [15:0] reg7,
  output [15:0] sval,
  output [15:0] tval
);

  wire demultiplexer_1_out0, demultiplexer_1_out1, demultiplexer_1_out2, demultiplexer_1_out3,
       demultiplexer_1_out4, demultiplexer_1_out5, demultiplexer_1_out6, demultiplexer_1_out7;

  Demultiplexer #(.select(3)) demultiplexer_1 (
    .out0(demultiplexer_1_out0), .out1(demultiplexer_1_out1), .out2(demultiplexer_1_out2),
    .out3(demultiplexer_1_out3), .out4(demultiplexer_1_out4), .out5(demultiplexer_1_out5),
    .out6(demultiplexer_1_out6), .out7(demultiplexer_1_out7), .in(dset), .sel(dreg));  // open: en
  Register #(.width(16)) register_1 (.D(dval), .en(demultiplexer_1_out0), .Q(reg0), .clk(clock));  // open: clr
  Register #(.width(16)) register_2 (.D(dval), .en(demultiplexer_1_out1), .Q(reg1), .clk(clock));  // open: clr
  Register #(.width(16)) register_3 (.D(dval), .en(demultiplexer_1_out2), .Q(reg2), .clk(clock));  // open: clr
  Register #(.width(16)) register_4 (.D(dval), .en(demultiplexer_1_out3), .Q(reg3), .clk(clock));  // open: clr
  Register #(.width(16)) register_5 (.D(dval), .en(demultiplexer_1_out4), .Q(reg4), .clk(clock));  // open: clr
  Register #(.width(16)) register_6 (.D(dval), .en(demultiplexer_1_out5), .Q(reg5), .clk(clock));  // open: clr
  Register #(.width(16)) register_7 (.D(dval), .en(demultiplexer_1_out6), .Q(reg6), .clk(clock));  // open: clr
  Register #(.width(16)) register_8 (.D(dval), .en(demultiplexer_1_out7), .Q(reg7), .clk(clock));  // open: clr
  Multiplexer #(.select(3), .width(16)) multiplexer_1 (
    .in0(reg0), .in1(reg1), .in2(reg2), .in3(reg3), .in4(reg4), .in5(reg5), .in6(reg6), .in7(reg7),
    .out(sval), .sel(sreg));  // open: en
  Multiplexer #(.select(3), .width(16)) multiplexer_2 (
    .in0(reg0), .in1(reg1), .in2(reg2), .in3(reg3), .in4(reg4), .in5(reg5), .in6(reg6), .in7(reg7),
    .out(tval), .sel(treg));  // open: en
  // Probe on reg0
  // Probe on reg1
  // Probe on reg2
  // Probe on reg3
  // Probe on reg4
  // Probe on reg5
  // Probe on reg6
  // Probe on reg7
endmodule

module alu_16bit (
  input  cin,
  input  [15:0] sval,
  input  sinv,
  input  [3:0] aop,
  input  [15:0] tval,
  input  tinv,
  output gt,
  output eq,
  output lt,
  output cout,
  output zero,
  output [15:0] dval
);

  wire [15:0] adder_1_out, and_1_out, bit_extender_1_out, bit_extender_2_out, bit_extender_3_out,
       invertmux_16bit_1_dval, invertmux_16bit_2_dval, or_1_out, shifter_1_out, shifter_2_out, xor_1_out;

  invertmux_16bit invertmux_16bit_1 (.sval(sval), .invert(sinv), .dval(invertmux_16bit_1_dval));
  invertmux_16bit invertmux_16bit_2 (.sval(tval), .invert(tinv), .dval(invertmux_16bit_2_dval));
  Comparator #(.width(16)) comparator_1 (
    .a(invertmux_16bit_1_dval), .b(invertmux_16bit_2_dval), .gt(gt), .eq(eq), .lt(lt));
  Adder #(.width(16)) adder_1 (
    .a(invertmux_16bit_1_dval), .b(invertmux_16bit_2_dval), .out(adder_1_out), .cin(cin), .cout(cout));
  assign and_1_out = invertmux_16bit_1_dval & invertmux_16bit_2_dval;  // AND_Gate and_1, 16 bits wide
  assign or_1_out = invertmux_16bit_1_dval | invertmux_16bit_2_dval;  // OR_Gate or_1, 16 bits wide
  assign xor_1_out = invertmux_16bit_1_dval ^ invertmux_16bit_2_dval;  // XOR_Gate xor_1, 16 bits wide
  assign bit_extender_1_out = {{15{1'b0}}, lt};  // Bit_Extender bit_extender_1
  Shifter #(.width(16)) shifter_1 (
    .in(invertmux_16bit_1_dval), .\dist (invertmux_16bit_2_dval[3:0]), .out(shifter_1_out));
  Shifter #(.width(16), .shift("lr")) shifter_2 (
    .in(invertmux_16bit_1_dval), .\dist (invertmux_16bit_2_dval[3:0]), .out(shifter_2_out));
  assign bit_extender_2_out = {{15{1'b0}}, eq};  // Bit_Extender bit_extender_2
  assign bit_extender_3_out = {{15{1'b0}}, gt};  // Bit_Extender bit_extender_3
  Multiplexer #(.select(4), .width(16)) multiplexer_1 (
    .in0(xor_1_out), .in1(or_1_out), .in2(and_1_out), .in3(shifter_2_out), .in4(shifter_1_out),
    .in5(adder_1_out), .in6(bit_extender_1_out), .in7(bit_extender_2_out), .in8(bit_extender_3_out),
    .out(dval), .sel(aop));  // open: in9, in10, in11, in12, in13, in14, in15, en
  or or_2 (zero, dval[0], dval[1], dval[2], dval[3], dval[4], dval[5], dval[6], dval[7], dval[9], dval[10], dval[11], dval[12], dval[13], dval[14], dval[15], dval[8]);
endmodule

module invertmux_16bit (
  input  [15:0] sval,
  input  invert,
  output [15:0] dval
);

  wire [15:0] not_1_out;

  assign not_1_out = ~sval;  // NOT_Gate not_1, 16 bits wide
  Multiplexer #(.width(16)) multiplexer_1 (.in0(not_1_out), .in1(sval), .out(dval), .sel(invert));  // open: en
endmodule

module pc_16bit (
  input  [1:0] pcop,
  input  [15:0] addr,
  input  pcset,
  input  clock,
  input  reset,
  output [15:0] pc,
  output [15:0] pc_1
);

  wire [15:0] adder_1_out, adder_2_out, multiplexer_1_out;

  Adder #(.width(16)) adder_1 (.a(pc), .b(16'h1), .out(adder_1_out));  // open: cin, cout
  Adder #(.width(16)) adder_2 (.a(pc), .b(addr), .out(adder_2_out));  // open: cin, cout
  Multiplexer #(.select(2), .width(16)) multiplexer_1 (
    .in0(adder_1_out), .in1(adder_2_out), .in2(addr), .out(multiplexer_1_out), .sel(pcop));  // open: in3, en
  Register #(.width(16)) register_1 (.D(multiplexer_1_out), .en(pcset), .Q(pc), .clk(clock), .clr(reset));
  Adder #(.width(16)) adder_3 (.a(pc), .b(16'h1), .out(pc_1));  // open: cin, cout
endmodule

module id_16bit (
  input  [15:0] inst,
  input  fetch,
  input  clock,
  output [6:0] op,
  output [2:0] dreg,
  output [2:0] sreg,
  output [2:0] treg
);

  Register #(.width(16)) register_1 (.D(inst), .en(fetch), .Q({treg, sreg, dreg, op}), .clk(clock));  // open: clr
endmodule

module cu_7bit (
  input  [6:0] cop,
  output ssel,
  output tsel,
  output cin,
  output sinv,
  output tinv,
  output [3:0] aop,
  output dset,
  output fset,
  output iset,
  output fetch,
  output pcload,
  output [1:0] pcop,
  output write,
  output [1:0] dsel,
  output timm
);

  wire [31:20] rom_1_data;

  // Probe on {1'b0, cop}
  ROM #(.dataWidth(32)) rom_1 (
    .addr({1'b0, cop}),
    .data({rom_1_data, timm, dsel, write, pcop, pcload, fetch, iset, fset, dset, aop, tinv, sinv, cin, tsel, ssel}));  // open: sel
  // Probe on {rom_1_data, timm, dsel, write, pcop, pcload, fetch, iset, fset, dset, aop, tinv, sinv, cin, tsel, ssel}

  // Notes on the sheet:
  //   cop: pull=down
  //   contents of rom_1 (hex, n*v repeats v):
  //   3000 3800 30a1
endmodule

module fu (
  input  gt,
  input  eq,
  input  lt,
  input  fset,
  input  cout,
  input  clock,
  input  zero,
  input  br,
  output gt_2,
  output eq_2,
  output lt_2,
  output cout_2,
  output zero_2,
  output br_2
);

  wire [7:6] flags_q;

  Register flags (
    .D({2'b00, br, zero, cout, lt, eq, gt}), .en(fset),
    .Q({flags_q, br_2, zero_2, cout_2, lt_2, eq_2, gt_2}), .clk(clock));  // open: clr
endmodule
